// Logisim project CPU.circ as structural Verilog
module OneBitAdder (
  input  A,
  input  B,
  input  C_in,
  output Sum,
  output C_out
);

  wire not_1_out, not_2_out, or_1_out, or_2_out, xor_1_out;

  xor xor_1 (xor_1_out, B, C_in);
  xor xor_2 (Sum, A, xor_1_out);
  not not_1 (not_1_out, Sum);
  not not_2 (not_2_out, xor_1_out);
  or or_1 (or_1_out, not_1_out, not_2_out);
  or or_2 (or_2_out, B, C_in);
  and and_1 (C_out, or_1_out, or_2_out);
endmodule

module FourBitAdder (
  input  A3,
  input  A2,
  input  A1,
  input  A0,
  input  B3,
  input  B2,
  input  B1,
  input  B0,
  output O,
  output X3,
  output X2,
  output X1,
  output X0
);

  wire onebitadder_2_c_out, onebitadder_3_c_out, onebitadder_4_c_out;

  OneBitAdder onebitadder_1 (.A(A3), .B(B3), .C_in(onebitadder_2_c_out), .Sum(X3), .C_out(O));
  OneBitAdder onebitadder_2 (.A(A2), .B(B2), .C_in(onebitadder_3_c_out), .Sum(X2), .C_out(onebitadder_2_c_out));
  OneBitAdder onebitadder_3 (.A(A1), .B(B1), .C_in(onebitadder_4_c_out), .Sum(X1), .C_out(onebitadder_3_c_out));
  OneBitAdder onebitadder_4 (.A(A0), .B(B0), .Sum(X0), .C_out(onebitadder_4_c_out));  // open: C_in
endmodule

module FourBitInverter (
  input  A3,
  input  A2,
  input  A1,
  input  A0,
  output Y3,
  output Y2,
  output Y1,
  output Y0
);

  not not_1 (Y3, A3);
  not not_2 (Y2, A2);
  not not_3 (Y1, A1);
  not not_4 (Y0, A0);
endmodule

module FourBitSubtractor (
  input  A3,
  input  A2,
  input  A1,
  input  A0,
  input  B3,
  input  B2,
  input  B1,
  input  B0,
  output X3,
  output X2,
  output X1,
  output X0
);

  wire fourbitadder_1_x0, fourbitadder_1_x1, fourbitadder_1_x2, fourbitadder_1_x3, fourbitinverter_1_y0,
       fourbitinverter_1_y1, fourbitinverter_1_y2, fourbitinverter_1_y3;

  FourBitInverter fourbitinverter_1 (
    .A3(B3), .A2(B2), .A1(B1), .A0(B0), .Y3(fourbitinverter_1_y3), .Y2(fourbitinverter_1_y2),
    .Y1(fourbitinverter_1_y1), .Y0(fourbitinverter_1_y0));
  FourBitAdder fourbitadder_1 (
    .A3(1'b0), .A2(1'b0), .A1(1'b0), .A0(1'b1), .B3(fourbitinverter_1_y3), .B2(fourbitinverter_1_y2),
    .B1(fourbitinverter_1_y1), .B0(fourbitinverter_1_y0), .X3(fourbitadder_1_x3), .X2(fourbitadder_1_x2),
    .X1(fourbitadder_1_x1), .X0(fourbitadder_1_x0));  // open: O
  FourBitAdder fourbitadder_2 (
    .A3(A3), .A2(A2), .A1(A1), .A0(A0), .B3(fourbitadder_1_x3), .B2(fourbitadder_1_x2),
    .B1(fourbitadder_1_x1), .B0(fourbitadder_1_x0), .X3(X3), .X2(X2), .X1(X1), .X0(X0));  // open: O
endmodule

module FourBitBuffer (
  input  D3,
  input  D2,
  input  D1,
  input  D0,
  input  S,
  output Y3,
  output Y2,
  output Y1,
  output Y0
);

  assign Y3 = S ? D3 : 1'bz;  // Controlled_Buffer controlled_buffer_1
  assign Y2 = S ? D2 : 1'bz;  // Controlled_Buffer controlled_buffer_2
  assign Y1 = S ? D1 : 1'bz;  // Controlled_Buffer controlled_buffer_3
  assign Y0 = S ? D0 : 1'bz;  // Controlled_Buffer controlled_buffer_4
endmodule

module ALU (
  input  OP2,
  input  OP1,
  input  OP0,
  input  A3,
  input  A2,
  input  A1,
  input  A0,
  input  B3,
  input  B2,
  input  B1,
  input  B0,
  output Y3,
  output Y2,
  output Y1,
  output Y0
);

  wire fourbitbuffer_1_y0, fourbitbuffer_1_y1, fourbitbuffer_1_y2, fourbitbuffer_1_y3, fourbitbuffer_2_y0,
       fourbitbuffer_2_y1, fourbitbuffer_2_y2, fourbitbuffer_2_y3, threetoeightdemux_1_out1;

  FourBitBuffer fourbitbuffer_1 (
    .D3(B3), .D2(B2), .D1(B1), .D0(B0), .S(threetoeightdemux_1_out1), .Y3(fourbitbuffer_1_y3),
    .Y2(fourbitbuffer_1_y2), .Y1(fourbitbuffer_1_y1), .Y0(fourbitbuffer_1_y0));
  FourBitBuffer fourbitbuffer_2 (
    .D3(A3), .D2(A2), .D1(A1), .D0(A0), .S(threetoeightdemux_1_out1), .Y3(fourbitbuffer_2_y3),
    .Y2(fourbitbuffer_2_y2), .Y1(fourbitbuffer_2_y1), .Y0(fourbitbuffer_2_y0));
  ThreeToEightDemux threetoeightdemux_1 (
    .IN2(OP2), .IN1(OP1), .IN0(OP0), .OUT1(threetoeightdemux_1_out1));  // open: OUT0, OUT2, OUT3, OUT4, OUT5, OUT6, OUT7
  FourBitAdder fourbitadder_1 (
    .A3(fourbitbuffer_2_y3), .A2(fourbitbuffer_2_y2), .A1(fourbitbuffer_2_y1), .A0(fourbitbuffer_2_y0),
    .B3(fourbitbuffer_1_y3), .B2(fourbitbuffer_1_y2), .B1(fourbitbuffer_1_y1), .B0(fourbitbuffer_1_y0),
    .X3(Y3), .X2(Y2), .X1(Y1), .X0(Y0));  // open: O
  FourBitSubtractor fourbitsubtractor_1 ();  // open: A3, A2, A1, A0, B3, B2, B1, B0, X3, X2, X1, X0

  // Notes on the sheet:
  //   Operands
  //   Opcodes
  //   Results
endmodule

module ThreeToEightDemux (
  input  IN2,
  input  IN1,
  input  IN0,
  output OUT0,
  output OUT1,
  output OUT2,
  output OUT3,
  output OUT4,
  output OUT5,
  output OUT6,
  output OUT7
);

  wire not_1_out, not_2_out, not_3_out, not_4_out, not_5_out, not_6_out, not_7_out, not_8_out, not_9_out,
       not_10_out, not_11_out, not_12_out;

  not not_1 (not_1_out, IN2);
  not not_2 (not_2_out, IN1);
  not not_3 (not_3_out, IN0);
  not not_4 (not_4_out, IN2);
  not not_5 (not_5_out, IN1);
  not not_6 (not_6_out, IN2);
  not not_7 (not_7_out, IN0);
  not not_8 (not_8_out, IN2);
  not not_9 (not_9_out, IN1);
  not not_10 (not_10_out, IN0);
  not not_11 (not_11_out, IN1);
  not not_12 (not_12_out, IN0);
  and and_1 (OUT0, not_1_out, not_2_out, not_3_out);
  and and_2 (OUT1, not_4_out, not_5_out, IN0);
  and and_3 (OUT2, not_6_out, IN1, not_7_out);
  and and_4 (OUT3, not_8_out, IN1, IN0);
  and and_5 (OUT4, IN2, not_9_out, not_10_out);
  and and_6 (OUT5, IN2, not_11_out, IN0);
  and and_7 (OUT6, IN2, IN1, not_12_out);
  and and_8 (OUT7, IN2, IN1, IN0);
endmodule
